// Logisim project cpu.circ as structural Verilog: 10 circuits, main circuit main
module main (
  input  reset
);

  wire ALU_input, and_1_out, branch_1, branch_2, clk, DMWE, keyboard_1_avail, memory_latch_1_oe_latched,
       memory_latch_1_we_latched, my_keyboard, my_tty, not_1_out, not_2_out, not_3_out, not_4_out, RWE;
  wire [1:0] jump, RD_RS_RT, RWD;
  wire [2:0] multiplexer_4_out, rd, rs, rt, shamt;
  wire [3:0] opcode;
  wire [5:0] immediate;
  wire [6:0] keyboard_1_data, keyboard_output;
  wire [7:0] multiplexer_1_out;
  wire [11:0] address;
  wire [15:0] data, ext_address, ext_immediate, keyboard_input, link, memory_latch_1_address_latched,
       memory_latch_1_data_in_latched, multiplexer_2_out, multiplexer_3_out, multiplexer_5_out,
       multiplexer_6_out, my16bitadder_1_result, myalu_1_my_output, PC_out_4, ram_1_dout, register_1,
       rom_1_data;

  Clock u_clk (.out(clk));
  Keyboard keyboard_1 (
    .clk(not_1_out), .re(my_keyboard), .clr(reset), .avail(keyboard_1_avail), .data(keyboard_1_data));
  not not_1 (not_1_out, clk);
  TTY #(.rows(13), .cols(80)) tty_1 (.data(keyboard_output), .clk(clk), .we(my_tty), .clr(reset));
  not not_2 (not_2_out, clk);
  Multiplexer #(.width(8), .enable("false")) multiplexer_1 (
    .in0({1'b0, keyboard_1_data}), .in1(8'h80), .out(multiplexer_1_out), .sel(not_3_out));
  not not_3 (not_3_out, keyboard_1_avail);
  assign keyboard_input = {{8{multiplexer_1_out[7]}}, multiplexer_1_out};  // Bit_Extender bit_extender_1
  myRegister PC (.clk(not_2_out), .reset(reset), .in_3(multiplexer_3_out), .out_4(PC_out_4));
  ROM #(.addrWidth(16), .dataWidth(16)) rom_1 (.addr(PC_out_4), .data(rom_1_data));
  my16BitAdder Add_4 (.B(PC_out_4), .A(16'h1), .sub(1'b0), .result(link));  // open: overflow
  and and_1 (and_1_out, branch_1, branch_2);
  assign ext_immediate = {{10{immediate[5]}}, immediate};  // Bit_Extender bit_extender_2
  assign ext_address = {{4{address[11]}}, address};  // Bit_Extender bit_extender_3
  Bit_Extender #(.in_width(16), .out_width(7)) bit_extender_4 (.in(register_1), .out(keyboard_output));
  Multiplexer #(.width(16), .enable("false")) multiplexer_2 (
    .in0(link), .in1(my16bitadder_1_result), .out(multiplexer_2_out), .sel(and_1_out));
  my16BitAdder my16bitadder_1 (
    .B(link), .A(ext_immediate), .sub(1'b0), .result(my16bitadder_1_result));  // open: overflow
  myInstructionDecoder myinstructiondecoder_1 (
    .instruction(rom_1_data), .tty(my_tty), .keyboard(my_keyboard), .opcode(opcode), .shamt(shamt),
    .branch(branch_1), .rd(rd), .RWE(RWE), .RWD(RWD), .rt(rt), .ALU_input(ALU_input), .RD_RS_RT(RD_RS_RT),
    .DMWE(DMWE), .rs(rs), .jump(jump), .immediate(immediate), .address(address));
  // Probe on keyboard_output
  // Probe on immediate
  Multiplexer #(.select(2), .width(16), .enable("false")) multiplexer_3 (
    .in0(multiplexer_2_out), .in1(ext_address), .in2(register_1), .out(multiplexer_3_out), .sel(jump));  // open: in3
  Multiplexer #(.select(2), .width(3), .enable("false")) multiplexer_4 (
    .in0(rd), .in1(rt), .in2(3'b111), .out(multiplexer_4_out), .sel(RD_RS_RT));  // open: in3
  // Probe on rt
  // Probe on ext_address
  // Probe on rd
  RegisterFile registerfile_1 (
    .RWE(RWE), .myInput(multiplexer_6_out), .reset(reset), .clk(clk), .rs1(rs), .rd(multiplexer_4_out),
    .rs2(rt), .output1(register_1), .output2(data));
  Multiplexer #(.width(16), .enable("false")) multiplexer_5 (
    .in0(data), .in1(ext_immediate), .out(multiplexer_5_out), .sel(ALU_input));
  myALU myalu_1 (
    .rs(register_1), .rt(multiplexer_5_out), .shamt(shamt), .op_code(opcode), .branch_2(branch_2),
    .my_output(myalu_1_my_output));
  not not_4 (not_4_out, clk);
  Multiplexer #(.select(2), .width(16), .enable("false")) multiplexer_6 (
    .in0(myalu_1_my_output), .in1(ram_1_dout), .in2(link), .in3(keyboard_input), .out(multiplexer_6_out),
    .sel(RWD));
  memory_latch memory_latch_1 (
    .address(myalu_1_my_output), .WE(DMWE), .clk(not_4_out), .data_in(data),
    .address_latched(memory_latch_1_address_latched), .WE_latched(memory_latch_1_we_latched),
    .OE_latched(memory_latch_1_oe_latched), .data_in_latched(memory_latch_1_data_in_latched));
  RAM #(.addrWidth(16), .dataWidth(16), .trigger("high"), .databus("bibus")) ram_1 (
    .addr(memory_latch_1_address_latched), .we(memory_latch_1_we_latched), .oe(memory_latch_1_oe_latched),
    .din(memory_latch_1_data_in_latched), .dout(ram_1_dout));

  // Other names for the same wires on the sheet: temp_output_instruction[15:0] = register_1
endmodule

module myRegister (
  input  clk,
  input  reset,
  input  [15:0] in_3,
  output [15:0] out_4
);

  D_Flip_Flop d_ff_1 (.D(in_3[0]), .clk(clk), .Q(out_4[0]), .reset(reset));  // open: Qn, preset
  D_Flip_Flop d_ff_2 (.D(in_3[1]), .clk(clk), .Q(out_4[1]), .reset(reset));  // open: Qn, preset
  D_Flip_Flop d_ff_3 (.D(in_3[2]), .clk(clk), .Q(out_4[2]), .reset(reset));  // open: Qn, preset
  D_Flip_Flop d_ff_4 (.D(in_3[3]), .clk(clk), .Q(out_4[3]), .reset(reset));  // open: Qn, preset
  D_Flip_Flop d_ff_5 (.D(in_3[4]), .clk(clk), .Q(out_4[4]), .reset(reset));  // open: Qn, preset
  D_Flip_Flop d_ff_6 (.D(in_3[5]), .clk(clk), .Q(out_4[5]), .reset(reset));  // open: Qn, preset
  D_Flip_Flop d_ff_7 (.D(in_3[6]), .clk(clk), .Q(out_4[6]), .reset(reset));  // open: Qn, preset
  D_Flip_Flop d_ff_8 (.D(in_3[7]), .clk(clk), .Q(out_4[7]), .reset(reset));  // open: Qn, preset
  D_Flip_Flop d_ff_9 (.D(in_3[8]), .clk(clk), .Q(out_4[8]), .reset(reset));  // open: Qn, preset
  D_Flip_Flop d_ff_10 (.D(in_3[9]), .clk(clk), .Q(out_4[9]), .reset(reset));  // open: Qn, preset
  D_Flip_Flop d_ff_11 (.D(in_3[10]), .clk(clk), .Q(out_4[10]), .reset(reset));  // open: Qn, preset
  D_Flip_Flop d_ff_12 (.D(in_3[11]), .clk(clk), .Q(out_4[11]), .reset(reset));  // open: Qn, preset
  D_Flip_Flop d_ff_13 (.D(in_3[12]), .clk(clk), .Q(out_4[12]), .reset(reset));  // open: Qn, preset
  D_Flip_Flop d_ff_14 (.D(in_3[13]), .clk(clk), .Q(out_4[13]), .reset(reset));  // open: Qn, preset
  D_Flip_Flop d_ff_15 (.D(in_3[14]), .clk(clk), .Q(out_4[14]), .reset(reset));  // open: Qn, preset
  D_Flip_Flop d_ff_16 (.D(in_3[15]), .clk(clk), .Q(out_4[15]), .reset(reset));  // open: Qn, preset

  // Other names for the same wires on the sheet: D0 = in_3[0]; D1 = in_3[1]; D2 = in_3[2]; D3 = in_3[3]; D4 = in_3[4];
  //   D5 = in_3[5]; D6 = in_3[6]; D7 = in_3[7]; D8 = in_3[8]; D9 = in_3[9]; D10 = in_3[10]; D11 = in_3[11];
  //   D12 = in_3[12]; D13 = in_3[13]; D14 = in_3[14]; D15 = in_3[15]
endmodule

module RegisterFile (
  input  RWE,
  input  [15:0] myInput,
  input  reset,
  input  clk,
  input  [2:0] rs1,
  input  [2:0] rd,
  input  [2:0] rs2,
  output [15:0] output1,
  output [15:0] output2
);

  wire and_1_out, and_2_out, and_3_out, and_4_out, and_5_out, and_6_out, and_7_out, decoder_1_out1,
       decoder_1_out2, decoder_1_out3, decoder_1_out4, decoder_1_out5, decoder_1_out6, decoder_1_out7,
       decoder_3_out0, decoder_3_out1, decoder_3_out2, decoder_3_out3, decoder_3_out4, decoder_3_out5,
       decoder_3_out6, decoder_3_out7, rs10, rs11, rs12, rs13, rs14, rs15, rs16, rs17;
  wire [15:0] myregister_1_out_4, myregister_2_out_4, myregister_3_out_4, myregister_4_out_4,
       myregister_5_out_4, myregister_6_out_4, myregister_7_out_4, myregister_8_out_4;

  Decoder #(.select(3)) decoder_1 (
    .out1(decoder_1_out1), .out2(decoder_1_out2), .out3(decoder_1_out3), .out4(decoder_1_out4),
    .out5(decoder_1_out5), .out6(decoder_1_out6), .out7(decoder_1_out7), .sel(rd));  // open: out0, en
  and and_1 (and_1_out, RWE, decoder_1_out1, clk);
  and and_2 (and_2_out, RWE, decoder_1_out2, clk);
  and and_3 (and_3_out, RWE, decoder_1_out3, clk);
  and and_4 (and_4_out, RWE, decoder_1_out4, clk);
  and and_5 (and_5_out, RWE, decoder_1_out5, clk);
  and and_6 (and_6_out, RWE, decoder_1_out6, clk);
  and and_7 (and_7_out, RWE, decoder_1_out7, clk);
  // Probe on myregister_1_out_4
  myRegister myregister_1 (.clk(clk), .reset(reset), .in_3({16{1'b0}}), .out_4(myregister_1_out_4));
  // Probe on myregister_2_out_4
  myRegister myregister_2 (.clk(and_1_out), .reset(reset), .in_3(myInput), .out_4(myregister_2_out_4));
  // Probe on myregister_3_out_4
  myRegister myregister_3 (.clk(and_2_out), .reset(reset), .in_3(myInput), .out_4(myregister_3_out_4));
  // Probe on myregister_4_out_4
  myRegister myregister_4 (.clk(and_3_out), .reset(reset), .in_3(myInput), .out_4(myregister_4_out_4));
  // Probe on myregister_5_out_4
  myRegister myregister_5 (.clk(and_4_out), .reset(reset), .in_3(myInput), .out_4(myregister_5_out_4));
  // Probe on myregister_6_out_4
  myRegister myregister_6 (.clk(and_5_out), .reset(reset), .in_3(myInput), .out_4(myregister_6_out_4));
  // Probe on myregister_7_out_4
  myRegister myregister_7 (.clk(and_6_out), .reset(reset), .in_3(myInput), .out_4(myregister_7_out_4));
  // Probe on myregister_8_out_4
  myRegister myregister_8 (.clk(and_7_out), .reset(reset), .in_3(myInput), .out_4(myregister_8_out_4));
  assign output1 = rs10 ? myregister_1_out_4 : 16'bz;  // Controlled_Buffer controlled_buffer_1
  assign output2 = decoder_3_out0 ? myregister_1_out_4 : 16'bz;  // Controlled_Buffer controlled_buffer_2
  assign output1 = rs11 ? myregister_2_out_4 : 16'bz;  // Controlled_Buffer controlled_buffer_3
  assign output2 = decoder_3_out1 ? myregister_2_out_4 : 16'bz;  // Controlled_Buffer controlled_buffer_4
  assign output1 = rs12 ? myregister_3_out_4 : 16'bz;  // Controlled_Buffer controlled_buffer_5
  assign output2 = decoder_3_out2 ? myregister_3_out_4 : 16'bz;  // Controlled_Buffer controlled_buffer_6
  assign output1 = rs13 ? myregister_4_out_4 : 16'bz;  // Controlled_Buffer controlled_buffer_7
  assign output2 = decoder_3_out3 ? myregister_4_out_4 : 16'bz;  // Controlled_Buffer controlled_buffer_8
  assign output1 = rs14 ? myregister_5_out_4 : 16'bz;  // Controlled_Buffer controlled_buffer_9
  assign output2 = decoder_3_out4 ? myregister_5_out_4 : 16'bz;  // Controlled_Buffer controlled_buffer_10
  assign output1 = rs15 ? myregister_6_out_4 : 16'bz;  // Controlled_Buffer controlled_buffer_11
  assign output2 = decoder_3_out5 ? myregister_6_out_4 : 16'bz;  // Controlled_Buffer controlled_buffer_12
  assign output1 = rs16 ? myregister_7_out_4 : 16'bz;  // Controlled_Buffer controlled_buffer_13
  assign output2 = decoder_3_out6 ? myregister_7_out_4 : 16'bz;  // Controlled_Buffer controlled_buffer_14
  assign output1 = rs17 ? myregister_8_out_4 : 16'bz;  // Controlled_Buffer controlled_buffer_15
  assign output2 = decoder_3_out7 ? myregister_8_out_4 : 16'bz;  // Controlled_Buffer controlled_buffer_16
  Decoder #(.select(3)) decoder_2 (
    .out0(rs10), .out1(rs11), .out2(rs12), .out3(rs13), .out4(rs14), .out5(rs15), .out6(rs16), .out7(rs17),
    .sel(rs1));  // open: en
  Decoder #(.select(3)) decoder_3 (
    .out0(decoder_3_out0), .out1(decoder_3_out1), .out2(decoder_3_out2), .out3(decoder_3_out3),
    .out4(decoder_3_out4), .out5(decoder_3_out5), .out6(decoder_3_out6), .out7(decoder_3_out7), .sel(rs2));  // open: en
endmodule

module myOneBitAdder (
  input  in_1,
  input  in_2,
  input  in_3,
  output out_4,
  output out_5
);

  wire and_1_out, and_2_out, xor_1_out;

  and and_1 (and_1_out, in_1, in_2);
  xor xor_1 (xor_1_out, in_1, in_2);
  or or_1 (out_5, and_1_out, and_2_out);
  and and_2 (and_2_out, xor_1_out, in_3);
  xor xor_2 (out_4, in_3, xor_1_out);

  // Other names for the same wires on the sheet: Cin = in_3; Cout = out_5
endmodule

module my16BitAdder (
  input  [15:0] B,
  input  [15:0] A,
  input  sub,
  output [15:0] result,
  output overflow
);

  wire myonebitadder_1_out_5, myonebitadder_2_out_5, myonebitadder_3_out_5, myonebitadder_4_out_5,
       myonebitadder_5_out_5, myonebitadder_6_out_5, myonebitadder_7_out_5, myonebitadder_8_out_5,
       myonebitadder_9_out_5, myonebitadder_10_out_5, myonebitadder_11_out_5, myonebitadder_12_out_5,
       myonebitadder_13_out_5, myonebitadder_14_out_5, myonebitadder_15_out_5, myonebitadder_16_out_5,
       xor_1_out, xor_2_out, xor_3_out, xor_4_out, xor_5_out, xor_6_out, xor_7_out, xor_8_out, xor_9_out,
       xor_10_out, xor_11_out, xor_12_out, xor_13_out, xor_14_out, xor_15_out, xor_16_out;

  myOneBitAdder myonebitadder_1 (
    .in_1(xor_1_out), .in_2(A[0]), .in_3(sub), .out_4(result[0]), .out_5(myonebitadder_1_out_5));
  xor xor_1 (xor_1_out, sub, B[0]);
  myOneBitAdder myonebitadder_2 (
    .in_1(xor_2_out), .in_2(A[1]), .in_3(myonebitadder_1_out_5), .out_4(result[1]),
    .out_5(myonebitadder_2_out_5));
  xor xor_2 (xor_2_out, sub, B[1]);
  myOneBitAdder myonebitadder_3 (
    .in_1(xor_3_out), .in_2(A[2]), .in_3(myonebitadder_2_out_5), .out_4(result[2]),
    .out_5(myonebitadder_3_out_5));
  xor xor_3 (xor_3_out, sub, B[2]);
  myOneBitAdder myonebitadder_4 (
    .in_1(xor_4_out), .in_2(A[3]), .in_3(myonebitadder_3_out_5), .out_4(result[3]),
    .out_5(myonebitadder_4_out_5));
  xor xor_4 (xor_4_out, sub, B[3]);
  myOneBitAdder myonebitadder_5 (
    .in_1(xor_5_out), .in_2(A[4]), .in_3(myonebitadder_4_out_5), .out_4(result[4]),
    .out_5(myonebitadder_5_out_5));
  xor xor_5 (xor_5_out, sub, B[4]);
  myOneBitAdder myonebitadder_6 (
    .in_1(xor_6_out), .in_2(A[5]), .in_3(myonebitadder_5_out_5), .out_4(result[5]),
    .out_5(myonebitadder_6_out_5));
  xor xor_6 (xor_6_out, sub, B[5]);
  myOneBitAdder myonebitadder_7 (
    .in_1(xor_7_out), .in_2(A[6]), .in_3(myonebitadder_6_out_5), .out_4(result[6]),
    .out_5(myonebitadder_7_out_5));
  xor xor_7 (xor_7_out, sub, B[6]);
  myOneBitAdder myonebitadder_8 (
    .in_1(xor_8_out), .in_2(A[7]), .in_3(myonebitadder_7_out_5), .out_4(result[7]),
    .out_5(myonebitadder_8_out_5));
  xor xor_8 (xor_8_out, sub, B[7]);
  myOneBitAdder myonebitadder_9 (
    .in_1(xor_9_out), .in_2(A[8]), .in_3(myonebitadder_8_out_5), .out_4(result[8]),
    .out_5(myonebitadder_9_out_5));
  xor xor_9 (xor_9_out, sub, B[8]);
  myOneBitAdder myonebitadder_10 (
    .in_1(xor_10_out), .in_2(A[9]), .in_3(myonebitadder_9_out_5), .out_4(result[9]),
    .out_5(myonebitadder_10_out_5));
  xor xor_10 (xor_10_out, sub, B[9]);
  myOneBitAdder myonebitadder_11 (
    .in_1(xor_11_out), .in_2(A[10]), .in_3(myonebitadder_10_out_5), .out_4(result[10]),
    .out_5(myonebitadder_11_out_5));
  xor xor_11 (xor_11_out, sub, B[10]);
  myOneBitAdder myonebitadder_12 (
    .in_1(xor_12_out), .in_2(A[11]), .in_3(myonebitadder_11_out_5), .out_4(result[11]),
    .out_5(myonebitadder_12_out_5));
  xor xor_12 (xor_12_out, sub, B[11]);
  myOneBitAdder myonebitadder_13 (
    .in_1(xor_13_out), .in_2(A[12]), .in_3(myonebitadder_12_out_5), .out_4(result[12]),
    .out_5(myonebitadder_13_out_5));
  xor xor_13 (xor_13_out, sub, B[12]);
  myOneBitAdder myonebitadder_14 (
    .in_1(xor_14_out), .in_2(A[13]), .in_3(myonebitadder_13_out_5), .out_4(result[13]),
    .out_5(myonebitadder_14_out_5));
  xor xor_14 (xor_14_out, sub, B[13]);
  myOneBitAdder myonebitadder_15 (
    .in_1(xor_15_out), .in_2(A[14]), .in_3(myonebitadder_14_out_5), .out_4(result[14]),
    .out_5(myonebitadder_15_out_5));
  xor xor_15 (xor_15_out, sub, B[14]);
  myOneBitAdder myonebitadder_16 (
    .in_1(xor_16_out), .in_2(A[15]), .in_3(myonebitadder_15_out_5), .out_4(result[15]),
    .out_5(myonebitadder_16_out_5));
  xor xor_16 (xor_16_out, sub, B[15]);
  xor xor_17 (overflow, myonebitadder_15_out_5, myonebitadder_16_out_5);

  // Other names for the same wires on the sheet: B1 = A[0]; B2 = A[1]; B3 = A[2]; B4 = A[3]; B5 = A[4]; B6 = A[5];
  //   B7 = A[6]; B8 = A[7]; B9 = A[8]; B10 = A[9]; B11 = A[10]; B12 = A[11]; B13 = A[12]; B14 = A[13]; B15 = A[14];
  //   B16 = A[15]; A1 = B[0]; A2 = B[1]; A3 = B[2]; A4 = B[3]; A5 = B[4]; A6 = B[5]; A7 = B[6]; A8 = B[7]; A9 = B[8];
  //   A10 = B[9]; A11 = B[10]; A12 = B[11]; A13 = B[12]; A14 = B[13]; A15 = B[14]; A16 = B[15]; R1 = result[0];
  //   R2 = result[1]; R3 = result[2]; R4 = result[3]; R5 = result[4]; R6 = result[5]; R7 = result[6]; R8 = result[7];
  //   R9 = result[8]; R10 = result[9]; R11 = result[10]; R12 = result[11]; R13 = result[12]; R14 = result[13];
  //   R15 = result[14]; R16 = result[15]
endmodule

module myLeftShifter (
  input  [2:0] shift_amount,
  input  [15:0] my_input,
  output [15:0] my_output
);

  wire decoder_1_out0, decoder_1_out1, decoder_1_out2, decoder_1_out3, decoder_1_out4, decoder_1_out5,
       decoder_1_out6, decoder_1_out7;

  Decoder #(.select(3)) decoder_1 (
    .out0(decoder_1_out0), .out1(decoder_1_out1), .out2(decoder_1_out2), .out3(decoder_1_out3),
    .out4(decoder_1_out4), .out5(decoder_1_out5), .out6(decoder_1_out6), .out7(decoder_1_out7),
    .sel(shift_amount));  // open: en
  assign my_output = decoder_1_out0 ? my_input : 16'bz;  // Controlled_Buffer controlled_buffer_1
  assign my_output = decoder_1_out1 ? {my_input[14:0], 1'b0} : 16'bz;  // Controlled_Buffer controlled_buffer_2
  assign my_output = decoder_1_out2 ? {my_input[13:0], 2'b00} : 16'bz;  // Controlled_Buffer controlled_buffer_3
  assign my_output = decoder_1_out3 ? {my_input[12:0], 3'b000} : 16'bz;  // Controlled_Buffer controlled_buffer_4
  assign my_output = decoder_1_out4 ? {my_input[11:0], 4'b0000} : 16'bz;  // Controlled_Buffer controlled_buffer_5
  assign my_output = decoder_1_out5 ? {my_input[10:0], {5{1'b0}}} : 16'bz;  // Controlled_Buffer controlled_buffer_6
  assign my_output = decoder_1_out6 ? {my_input[9:0], {6{1'b0}}} : 16'bz;  // Controlled_Buffer controlled_buffer_7
  assign my_output = decoder_1_out7 ? {my_input[8:0], {7{1'b0}}} : 16'bz;  // Controlled_Buffer controlled_buffer_8
endmodule

module myRightShifter (
  input  [15:0] my_input,
  input  [2:0] shift_amount,
  output [15:0] my_output
);

  myLeftShifter myleftshifter_1 (
    .shift_amount(shift_amount),
    .my_input({my_input[0], my_input[1], my_input[2], my_input[3], my_input[4], my_input[5], my_input[6], my_input[7], my_input[8], my_input[9], my_input[10], my_input[11], my_input[12], my_input[13], my_input[14], my_input[15]}),
    .my_output({my_output[0], my_output[1], my_output[2], my_output[3], my_output[4], my_output[5], my_output[6], my_output[7], my_output[8], my_output[9], my_output[10], my_output[11], my_output[12], my_output[13], my_output[14], my_output[15]}));
endmodule

module myALU (
  input  [15:0] rs,
  input  [15:0] rt,
  input  [2:0] shamt,
  input  [3:0] op_code,
  output branch_2,
  output [15:0] my_output
);

  wire bgt_output, not_1_out;
  wire [14:0] my16bitadder_3_result;
  wire [15:0] add_output, and_output, beq_output, bit_extender_1_out, not_2_out, sll_output, srl_output,
       xor_output;

  assign and_output = rt & rs;  // AND_Gate and_1, 16 bits wide
  assign xor_output = rt ^ rs;  // XOR_Gate xor_1, 16 bits wide
  my16BitAdder my16bitadder_1 (.B(rt), .A(rs), .sub(1'b0), .result(add_output));  // open: overflow
  my16BitAdder my16bitadder_2 (.B(rt), .A(rs), .sub(1'b1), .result(beq_output));  // open: overflow
  myLeftShifter myleftshifter_1 (.shift_amount(shamt), .my_input(rs), .my_output(sll_output));
  myRightShifter myrightshifter_1 (.my_input(rs), .shift_amount(shamt), .my_output(srl_output));
  my16BitAdder my16bitadder_3 (
    .B(rs), .A(rt), .sub(1'b1), .result({bgt_output, my16bitadder_3_result}));  // open: overflow
  not not_1 (not_1_out, bgt_output);
  assign bit_extender_1_out = {{15{not_1_out}}, not_1_out};  // Bit_Extender bit_extender_1
  Multiplexer #(.select(4), .width(16), .enable("false")) multiplexer_1 (
    .in5(bit_extender_1_out), .in6(beq_output), .in7(add_output), .in8(add_output), .in9(xor_output),
    .in10(and_output), .in11(srl_output), .in12(sll_output), .in13(beq_output), .in14(add_output),
    .in15(add_output), .out(my_output), .sel(op_code));  // open: in0, in1, in2, in3, in4
  assign not_2_out = ~my_output;  // NOT_Gate not_2, 16 bits wide
  and and_2 (branch_2, not_2_out[0], not_2_out[1], not_2_out[2], not_2_out[3], not_2_out[4], not_2_out[5], not_2_out[6], not_2_out[7], not_2_out[8], not_2_out[9], not_2_out[10], not_2_out[11], not_2_out[12], not_2_out[13], not_2_out[14], not_2_out[15]);

  // Other names for the same wires on the sheet: sub_output[15:0] = beq_output; addi_output[15:0] = add_output;
  //   lw_output[15:0] = add_output; sw_output[15:0] = add_output
endmodule

module myInstructionDecoder (
  input  [15:0] instruction,
  output tty,
  output keyboard,
  output [3:0] opcode,
  output [2:0] shamt,
  output branch,
  output [2:0] rd,
  output RWE,
  output [1:0] RWD,
  output [2:0] rt,
  output ALU_input,
  output [1:0] RD_RS_RT,
  output DMWE,
  output [2:0] rs,
  output [1:0] jump,
  output [5:0] immediate,
  output [11:0] address
);

  wire add, addi, and_bba5b93e, beq, bgt, i_type, j, j_type, lw, or_1_out, or_2_out, r_type, sll_6ceba103,
       srl_202c7200, sub, xor_49925dc5;

  assign rs = or_1_out ? instruction[11:9] : 3'bz;  // Controlled_Buffer controlled_buffer_1
  or or_1 (or_1_out, r_type, i_type);
  assign shamt = r_type ? instruction[2:0] : 3'bz;  // Controlled_Buffer controlled_buffer_2
  assign rd = r_type ? instruction[5:3] : 3'bz;  // Controlled_Buffer controlled_buffer_3
  assign rt = or_2_out ? instruction[8:6] : 3'bz;  // Controlled_Buffer controlled_buffer_4
  or or_2 (or_2_out, r_type, i_type);
  assign immediate = i_type ? instruction[5:0] : 6'bz;  // Controlled_Buffer controlled_buffer_5
  assign address = j_type ? instruction[11:0] : 12'bz;  // Controlled_Buffer controlled_buffer_6
  or or_3 (jump[0], RD_RS_RT[1], j);
  Decoder #(.select(4)) decoder_1 (
    .out0(tty), .out1(keyboard), .out2(RD_RS_RT[1]), .out3(jump[1]), .out4(j), .out5(bgt), .out6(beq),
    .out7(DMWE), .out8(lw), .out9(xor_49925dc5), .out10(and_bba5b93e), .out11(srl_202c7200),
    .out12(sll_6ceba103), .out13(sub), .out14(addi), .out15(add), .sel(instruction[15:12]));  // open: en
  or or_4 (branch, bgt, beq);
  or or_5 (ALU_input, DMWE, lw, addi);
  or or_6 (RWE, keyboard, add, addi, sub, and_bba5b93e, xor_49925dc5, sll_6ceba103, srl_202c7200, lw, RD_RS_RT[1]);
  or or_7 (RD_RS_RT[0], keyboard, j, addi, j, bgt, beq, DMWE, lw);
  or or_8 (r_type, add, sub, sll_6ceba103, srl_202c7200, and_bba5b93e, xor_49925dc5, jump[1]);
  or or_9 (i_type, addi, lw, DMWE, beq, bgt, keyboard, tty);
  or or_10 (j_type, RD_RS_RT[1], j);
  or or_11 (RWD[0], lw, keyboard);
  or or_12 (RWD[1], keyboard, RD_RS_RT[1]);

  assign opcode = instruction[15:12];

  // Other names for the same wires on the sheet: in0 = instruction[0]; in1 = instruction[1]; in2 = instruction[2];
  //   in3 = instruction[3]; in4 = instruction[4]; in5 = instruction[5]; in6 = instruction[6]; in7 = instruction[7];
  //   in8 = instruction[8]; in9 = instruction[9]; in10 = instruction[10]; in11 = instruction[11];
  //   input_a707b43a = keyboard; jr = jump[1]; output_ad136bd8 = tty; jal = RD_RS_RT[1]; sw = DMWE
endmodule

module memory_latch (
  input  [15:0] address,
  input  WE,
  input  clk,
  input  [15:0] data_in,
  output [15:0] address_latched,
  output WE_latched,
  output OE_latched,
  output [15:0] data_in_latched
);

  wire DMwe_latch_q;
  wire [15:0] addr_latch_q;

  Register #(.width(16), .trigger("falling")) addr_latch (
    .D(address), .en(WE), .clk(clk), .Q(addr_latch_q));  // open: clr
  D_Flip_Flop #(.trigger("falling")) DMwe_latch (.D(WE), .clk(clk), .Q(DMwe_latch_q));  // open: Qn, preset, reset
  Register #(.width(16), .trigger("falling")) data_to_be_written (
    .D(data_in), .en(WE), .clk(clk), .Q(data_in_latched));  // open: clr
  Multiplexer #(.width(16), .enable("false")) multiplexer_1 (
    .in0(address), .in1(addr_latch_q), .out(address_latched), .sel(DMwe_latch_q));
  and and_1 (WE_latched, clk, DMwe_latch_q);
  not not_1 (OE_latched, WE_latched);
endmodule
