// Logisim project my_adder.circ as structural Verilog: 2 circuits, main circuit main
module main (
  input  [15:0] B,
  input  [15:0] A,
  input  sub,
  output [15:0] result,
  output ovf
);

  wire one_bit_1_cout, one_bit_2_cout, one_bit_3_cout, one_bit_4_cout, one_bit_5_cout, one_bit_6_cout,
       one_bit_7_cout, one_bit_8_cout, one_bit_9_cout, one_bit_10_cout, one_bit_11_cout, one_bit_12_cout,
       one_bit_13_cout, one_bit_14_cout, one_bit_15_cout, one_bit_16_cout, xor_1_out, xor_2_out, xor_3_out,
       xor_4_out, xor_5_out, xor_6_out, xor_7_out, xor_8_out, xor_9_out, xor_10_out, xor_11_out, xor_12_out,
       xor_13_out, xor_14_out, xor_15_out, xor_16_out;

  one_bit one_bit_1 (.my_A(xor_1_out), .my_B(A[0]), .Cin(sub), .my_result(result[0]), .Cout(one_bit_1_cout));
  xor xor_1 (xor_1_out, sub, B[0]);
  one_bit one_bit_2 (.my_A(xor_2_out), .my_B(A[1]), .Cin(one_bit_1_cout), .my_result(result[1]), .Cout(one_bit_2_cout));
  xor xor_2 (xor_2_out, sub, B[1]);
  one_bit one_bit_3 (.my_A(xor_3_out), .my_B(A[2]), .Cin(one_bit_2_cout), .my_result(result[2]), .Cout(one_bit_3_cout));
  xor xor_3 (xor_3_out, sub, B[2]);
  one_bit one_bit_4 (.my_A(xor_4_out), .my_B(A[3]), .Cin(one_bit_3_cout), .my_result(result[3]), .Cout(one_bit_4_cout));
  xor xor_4 (xor_4_out, sub, B[3]);
  one_bit one_bit_5 (.my_A(xor_5_out), .my_B(A[4]), .Cin(one_bit_4_cout), .my_result(result[4]), .Cout(one_bit_5_cout));
  xor xor_5 (xor_5_out, sub, B[4]);
  one_bit one_bit_6 (.my_A(xor_6_out), .my_B(A[5]), .Cin(one_bit_5_cout), .my_result(result[5]), .Cout(one_bit_6_cout));
  xor xor_6 (xor_6_out, sub, B[5]);
  one_bit one_bit_7 (.my_A(xor_7_out), .my_B(A[6]), .Cin(one_bit_6_cout), .my_result(result[6]), .Cout(one_bit_7_cout));
  xor xor_7 (xor_7_out, sub, B[6]);
  one_bit one_bit_8 (.my_A(xor_8_out), .my_B(A[7]), .Cin(one_bit_7_cout), .my_result(result[7]), .Cout(one_bit_8_cout));
  xor xor_8 (xor_8_out, sub, B[7]);
  one_bit one_bit_9 (.my_A(xor_9_out), .my_B(A[8]), .Cin(one_bit_8_cout), .my_result(result[8]), .Cout(one_bit_9_cout));
  xor xor_9 (xor_9_out, sub, B[8]);
  one_bit one_bit_10 (
    .my_A(xor_10_out), .my_B(A[9]), .Cin(one_bit_9_cout), .my_result(result[9]), .Cout(one_bit_10_cout));
  xor xor_10 (xor_10_out, sub, B[9]);
  one_bit one_bit_11 (
    .my_A(xor_11_out), .my_B(A[10]), .Cin(one_bit_10_cout), .my_result(result[10]), .Cout(one_bit_11_cout));
  xor xor_11 (xor_11_out, sub, B[10]);
  one_bit one_bit_12 (
    .my_A(xor_12_out), .my_B(A[11]), .Cin(one_bit_11_cout), .my_result(result[11]), .Cout(one_bit_12_cout));
  xor xor_12 (xor_12_out, sub, B[11]);
  one_bit one_bit_13 (
    .my_A(xor_13_out), .my_B(A[12]), .Cin(one_bit_12_cout), .my_result(result[12]), .Cout(one_bit_13_cout));
  xor xor_13 (xor_13_out, sub, B[12]);
  one_bit one_bit_14 (
    .my_A(xor_14_out), .my_B(A[13]), .Cin(one_bit_13_cout), .my_result(result[13]), .Cout(one_bit_14_cout));
  xor xor_14 (xor_14_out, sub, B[13]);
  one_bit one_bit_15 (
    .my_A(xor_15_out), .my_B(A[14]), .Cin(one_bit_14_cout), .my_result(result[14]), .Cout(one_bit_15_cout));
  xor xor_15 (xor_15_out, sub, B[14]);
  one_bit one_bit_16 (
    .my_A(xor_16_out), .my_B(A[15]), .Cin(one_bit_15_cout), .my_result(result[15]), .Cout(one_bit_16_cout));
  xor xor_16 (xor_16_out, sub, B[15]);
  xor xor_17 (ovf, one_bit_15_cout, one_bit_16_cout);

  // Other names for the same wires on the sheet: B1 = A[0]; B2 = A[1]; B3 = A[2]; B4 = A[3]; B5 = A[4]; B6 = A[5];
  //   B7 = A[6]; B8 = A[7]; B9 = A[8]; B10 = A[9]; B11 = A[10]; B12 = A[11]; B13 = A[12]; B14 = A[13]; B15 = A[14];
  //   B16 = A[15]; A1 = B[0]; A2 = B[1]; A3 = B[2]; A4 = B[3]; A5 = B[4]; A6 = B[5]; A7 = B[6]; A8 = B[7]; A9 = B[8];
  //   A10 = B[9]; A11 = B[10]; A12 = B[11]; A13 = B[12]; A14 = B[13]; A15 = B[14]; A16 = B[15]; R1 = result[0];
  //   R2 = result[1]; R3 = result[2]; R4 = result[3]; R5 = result[4]; R6 = result[5]; R7 = result[6]; R8 = result[7];
  //   R9 = result[8]; R10 = result[9]; R11 = result[10]; R12 = result[11]; R13 = result[12]; R14 = result[13];
  //   R15 = result[14]; R16 = result[15]
endmodule

module one_bit (
  input  my_A,
  input  my_B,
  input  Cin,
  output my_result,
  output Cout
);

  wire and_1_out, and_2_out, xor_1_out;

  and and_1 (and_1_out, my_A, my_B);
  xor xor_1 (xor_1_out, my_A, my_B);
  or or_1 (Cout, and_1_out, and_2_out);
  and and_2 (and_2_out, xor_1_out, Cin);
  xor xor_2 (my_result, Cin, xor_1_out);
endmodule
