// Logisim project robot.circ as structural Verilog: 1 circuit, main circuit main
module main (
  input  in_go,
  input  in_grab,
  input  override,
  output motion,
  output grabbing,
  output warning
);

  wire and_1_out, and_2_out, and_3_out, clk, not_1_out, not_2_out, not_3_out, not_4_out, not_5_out, not_Q0,
       or_1_out;

  Clock clock_1 (.out(clk));
  not not_1 (not_1_out, override);
  not not_2 (not_2_out, override);
  not not_3 (not_3_out, in_grab);
  and and_1 (and_1_out, not_Q0, not_1_out, in_grab);
  and and_2 (and_2_out, grabbing, not_2_out, not_3_out);
  not not_4 (not_4_out, override);
  or or_1 (or_1_out, and_1_out, and_2_out);
  D_Flip_Flop D1 (.D(and_3_out), .clk(clk), .Q(motion));  // open: Qn, preset, reset
  and and_3 (and_3_out, not_4_out, in_go);
  D_Flip_Flop D0 (.D(or_1_out), .clk(clk), .Q(grabbing), .Qn(not_Q0));  // open: preset, reset
  not not_5 (not_5_out, grabbing);
  and and_4 (warning, motion, not_5_out);

  // Other names for the same wires on the sheet: in0 = in_go; in1 = in_grab; in2 = override; Q0 = grabbing
endmodule
